// Logisim project adder.circ as structural Verilog: 3 circuits, main circuit main
module main (
  input  [31:0] A,
  input  sub,
  input  [31:0] B,
  output ovf,
  output [31:0] result
);

  wire adder_1_cout, adder_2_cout, adder_3_cout;

  Adder adder_1 (
    .sub(sub), .B(B[7:0]), .cin(sub), .A(A[7:0]), .cout(adder_1_cout), .result(result[7:0]));  // open: overflow
  Adder adder_2 (
    .sub(sub), .B(B[15:8]), .cin(adder_1_cout), .A(A[15:8]), .cout(adder_2_cout), .result(result[15:8]));  // open: overflow
  Adder adder_3 (
    .sub(sub), .B(B[23:16]), .cin(adder_2_cout), .A(A[23:16]), .cout(adder_3_cout), .result(result[23:16]));  // open: overflow
  Adder adder_4 (
    .sub(sub), .B(B[31:24]), .cin(adder_3_cout), .A(A[31:24]), .overflow(ovf), .result(result[31:24]));  // open: cout
endmodule

module _1bitadder (
  input  cin,
  input  A,
  input  B,
  output sum,
  output cout
);

  wire and_1_out, and_2_out, xor_1_out;

  and and_1 (and_1_out, A, B);
  xor xor_1 (xor_1_out, A, B);
  xor xor_2 (sum, cin, xor_1_out);
  and and_2 (and_2_out, cin, xor_1_out);
  or or_1 (cout, and_2_out, and_1_out);
endmodule

module Adder (
  input  sub,
  input  [7:0] B,
  input  cin,
  input  [7:0] A,
  output overflow,
  output cout,
  output [7:0] result
);

  wire n1bitadder_1_cout, n1bitadder_2_cout, n1bitadder_3_cout, n1bitadder_4_cout, n1bitadder_5_cout,
       n1bitadder_6_cout, n1bitadder_7_cout, xor_1_out, xor_2_out, xor_3_out, xor_4_out, xor_5_out,
       xor_6_out, xor_7_out, xor_8_out;

  _1bitadder u_1bitadder_1 (.cin(cin), .A(A[0]), .B(xor_1_out), .sum(result[0]), .cout(n1bitadder_1_cout));
  xor xor_1 (xor_1_out, B[0], sub);
  xor xor_2 (xor_2_out, B[1], sub);
  _1bitadder u_1bitadder_2 (
    .cin(n1bitadder_1_cout), .A(A[1]), .B(xor_2_out), .sum(result[1]), .cout(n1bitadder_2_cout));
  xor xor_3 (xor_3_out, B[2], sub);
  _1bitadder u_1bitadder_3 (
    .cin(n1bitadder_2_cout), .A(A[2]), .B(xor_3_out), .sum(result[2]), .cout(n1bitadder_3_cout));
  xor xor_4 (xor_4_out, sub, B[4]);
  xor xor_5 (xor_5_out, B[3], sub);
  _1bitadder u_1bitadder_4 (
    .cin(n1bitadder_3_cout), .A(A[3]), .B(xor_5_out), .sum(result[3]), .cout(n1bitadder_4_cout));
  xor xor_6 (xor_6_out, B[6], sub);
  xor xor_7 (xor_7_out, B[5], sub);
  _1bitadder u_1bitadder_5 (
    .cin(n1bitadder_4_cout), .A(A[4]), .B(xor_4_out), .sum(result[4]), .cout(n1bitadder_5_cout));
  xor xor_8 (xor_8_out, B[7], sub);
  _1bitadder u_1bitadder_6 (
    .cin(n1bitadder_5_cout), .A(A[5]), .B(xor_7_out), .sum(result[5]), .cout(n1bitadder_6_cout));
  _1bitadder u_1bitadder_7 (
    .cin(n1bitadder_6_cout), .A(A[6]), .B(xor_6_out), .sum(result[6]), .cout(n1bitadder_7_cout));
  _1bitadder u_1bitadder_8 (.cin(n1bitadder_7_cout), .A(A[7]), .B(xor_8_out), .sum(result[7]), .cout(cout));
  xor xor_9 (overflow, n1bitadder_7_cout, cout);
endmodule
