// Logisim project fsm.circ as structural Verilog: 3 circuits, main circuit main
module main (
  input  in1,
  input  in2,
  input  in3,
  output out1,
  output out2
);

  out1 out1_1 (.In1(in1), .In2(in2), .In3(in3), .out1(out1));
  outs outs_1 (.in1(in1), .in2(in2), .in3(in3), .out2(out2));
endmodule

// out1circ
module out1 (
  input  In1,
  input  In2,
  input  In3,
  output out1
);

  wire and_1_out, and_2_out, and_3_out, and_4_out, and_5_out, and_6_out, and_7_out, and_8_out, clk_out,
       D0_qn, not_1_out, not_2_out, not_3_out, or_1_out, or_2_out, or_3_out;

  not not_1 (not_1_out, In1);
  and and_1 (and_1_out, D0_qn, In3, In2, In1);
  not not_2 (not_2_out, In2);
  not not_3 (not_3_out, In3);
  and and_2 (and_2_out, out1, In1, In2, In3);
  and and_3 (and_3_out, In1, not_3_out, In2, D0_qn);
  and and_4 (and_4_out, In1, In2, not_3_out, out1);
  and and_5 (and_5_out, In1, not_2_out, In3, D0_qn);
  and and_6 (and_6_out, In1, not_2_out, In3, out1);
  and and_7 (and_7_out, not_1_out, In2, In3, D0_qn);
  and and_8 (and_8_out, not_1_out, In2, In3, out1);
  Clock clk (.out(clk_out));
  or or_1 (or_1_out, and_1_out, and_2_out, and_3_out, and_4_out, and_5_out);
  or or_2 (or_2_out, and_6_out, and_7_out, and_8_out);
  D_Flip_Flop D0 (.clk(clk_out), .D(or_3_out), .Q(out1), .Qn(D0_qn));  // open: preset, en, reset
  or or_3 (or_3_out, or_1_out, or_2_out);
endmodule

// out2circ
module outs (
  input  in1,
  input  in2,
  input  in3,
  output out2
);

  wire and_1_out, and_2_out, and_3_out, and_4_out, and_5_out, and_6_out, and_7_out, and_8_out, and_9_out,
       and_10_out, and_11_out, and_12_out, and_13_out, and_14_out, and_15_out, and_16_out, and_17_out,
       and_18_out, and_19_out, and_20_out, and_21_out, and_22_out, clk, not_1_out, not_2_out, not_3_out,
       or_1_out, or_2_out, or_3_out, or_4_out, or_5_out, or_6_out, or_7_out, or_8_out, or_9_out, or_10_out,
       or_11_out, Q0_q, Q0_qn, Q1_qn;

  not not_1 (not_1_out, in1);
  not not_2 (not_2_out, in2);
  not not_3 (not_3_out, in3);
  Clock u_clk (.out(clk));
  and and_1 (and_1_out, Q1_qn, Q0_q, in1, not_2_out, not_3_out);
  and and_2 (and_2_out, Q1_qn, Q0_q, not_1_out, not_2_out, in3);
  and and_3 (and_3_out, Q1_qn, Q0_q, not_1_out, in2, not_3_out);
  and and_4 (and_4_out, out2, Q0_qn, in1, not_2_out, not_3_out);
  and and_5 (and_5_out, out2, Q0_qn, not_1_out, not_2_out, in3);
  and and_6 (and_6_out, out2, Q0_qn, not_1_out, in2, not_3_out);
  D_Flip_Flop Q1 (.clk(clk), .D(or_11_out), .Q(out2), .Qn(Q1_qn));  // open: preset, en, reset
  D_Flip_Flop Q0 (.clk(clk), .D(or_10_out), .Q(Q0_q), .Qn(Q0_qn));  // open: preset, en, reset
  or or_1 (or_1_out, and_1_out, and_2_out, and_3_out, and_4_out);
  or or_2 (or_2_out, or_1_out, or_3_out);
  or or_3 (or_3_out, and_5_out, and_6_out);
  and and_7 (and_7_out, Q1_qn, Q0_q, not_1_out, not_2_out, not_3_out);
  and and_8 (and_8_out, Q1_qn, Q0_q, not_1_out, in2, in3);
  and and_9 (and_9_out, Q1_qn, Q0_q, in1, in2, not_3_out);
  and and_10 (and_10_out, Q1_qn, Q0_q, in1, in2, in3);
  and and_11 (and_11_out, Q1_qn, Q0_qn, in1, not_2_out, not_3_out);
  and and_12 (and_12_out, Q1_qn, Q0_qn, not_1_out, not_2_out, in3);
  and and_13 (and_13_out, Q1_qn, Q0_qn, not_1_out, in2, not_3_out);
  and and_14 (and_14_out, out2, Q0_q, in1, not_2_out, not_3_out);
  and and_15 (and_15_out, out2, Q0_q, not_1_out, not_2_out, in3);
  and and_16 (and_16_out, out2, Q0_q, not_1_out, in2, not_3_out);
  and and_17 (and_17_out, Q1_qn, Q0_q, in1, not_2_out, in3);
  and and_18 (and_18_out, out2, Q0_qn, not_1_out, not_2_out, not_3_out);
  and and_19 (and_19_out, out2, Q0_qn, not_1_out, in2, in3);
  or or_4 (or_4_out, and_11_out, and_12_out, and_13_out, and_14_out);
  or or_5 (or_5_out, and_15_out, and_16_out);
  or or_6 (or_6_out, and_7_out, and_8_out, and_9_out, and_10_out, and_17_out);
  and and_20 (and_20_out, out2, Q0_qn, in1, in2, not_3_out);
  or or_7 (or_7_out, or_4_out, or_5_out);
  and and_21 (and_21_out, out2, Q0_qn, in1, in2, in3);
  and and_22 (and_22_out, out2, Q0_qn, in1, not_2_out, in3);
  or or_8 (or_8_out, and_18_out, and_19_out, and_20_out, and_21_out, and_22_out);
  or or_9 (or_9_out, or_6_out, or_8_out);
  or or_10 (or_10_out, or_9_out, or_7_out);
  or or_11 (or_11_out, or_9_out, or_2_out);
endmodule
