// Logisim project hw4.circ as structural Verilog: 18 circuits, main circuit main
module _1_bit_adder (
  input  cin,
  input  A,
  input  B,
  output sum,
  output cout
);

  wire and_1_out, and_2_out, xor_1_out;

  and and_1 (and_1_out, A, B);
  xor xor_1 (xor_1_out, A, B);
  xor xor_2 (sum, cin, xor_1_out);
  and and_2 (and_2_out, cin, xor_1_out);
  or or_1 (cout, and_2_out, and_1_out);
endmodule

module _8_bit_adder (
  input  sub,
  input  [7:0] B,
  input  cin,
  input  [7:0] A,
  output overflow,
  output cout,
  output [7:0] result
);

  wire n1_bit_adder_1_cout, n1_bit_adder_2_cout, n1_bit_adder_3_cout, n1_bit_adder_4_cout,
       n1_bit_adder_5_cout, n1_bit_adder_6_cout, n1_bit_adder_7_cout, xor_1_out, xor_2_out, xor_3_out,
       xor_4_out, xor_5_out, xor_6_out, xor_7_out, xor_8_out;

  _1_bit_adder u_1_bit_adder_1 (.cin(cin), .A(A[0]), .B(xor_1_out), .sum(result[0]), .cout(n1_bit_adder_1_cout));
  xor xor_1 (xor_1_out, B[0], sub);
  xor xor_2 (xor_2_out, B[1], sub);
  _1_bit_adder u_1_bit_adder_2 (
    .cin(n1_bit_adder_1_cout), .A(A[1]), .B(xor_2_out), .sum(result[1]), .cout(n1_bit_adder_2_cout));
  xor xor_3 (xor_3_out, B[2], sub);
  _1_bit_adder u_1_bit_adder_3 (
    .cin(n1_bit_adder_2_cout), .A(A[2]), .B(xor_3_out), .sum(result[2]), .cout(n1_bit_adder_3_cout));
  xor xor_4 (xor_4_out, sub, B[4]);
  xor xor_5 (xor_5_out, B[3], sub);
  _1_bit_adder u_1_bit_adder_4 (
    .cin(n1_bit_adder_3_cout), .A(A[3]), .B(xor_5_out), .sum(result[3]), .cout(n1_bit_adder_4_cout));
  xor xor_6 (xor_6_out, B[6], sub);
  xor xor_7 (xor_7_out, B[5], sub);
  _1_bit_adder u_1_bit_adder_5 (
    .cin(n1_bit_adder_4_cout), .A(A[4]), .B(xor_4_out), .sum(result[4]), .cout(n1_bit_adder_5_cout));
  xor xor_8 (xor_8_out, B[7], sub);
  _1_bit_adder u_1_bit_adder_6 (
    .cin(n1_bit_adder_5_cout), .A(A[5]), .B(xor_7_out), .sum(result[5]), .cout(n1_bit_adder_6_cout));
  _1_bit_adder u_1_bit_adder_7 (
    .cin(n1_bit_adder_6_cout), .A(A[6]), .B(xor_6_out), .sum(result[6]), .cout(n1_bit_adder_7_cout));
  _1_bit_adder u_1_bit_adder_8 (.cin(n1_bit_adder_7_cout), .A(A[7]), .B(xor_8_out), .sum(result[7]), .cout(cout));
  xor xor_9 (overflow, n1_bit_adder_7_cout, cout);
endmodule

module _16_bit_adder_subtractor (
  input  [15:0] A,
  input  sub,
  input  [15:0] B,
  output ovf,
  output [15:0] result
);

  wire n8_bit_adder_1_cout;

  _8_bit_adder u_8_bit_adder_1 (
    .sub(sub), .B(B[7:0]), .cin(sub), .A(A[7:0]), .cout(n8_bit_adder_1_cout), .result(result[7:0]));  // open: overflow
  _8_bit_adder u_8_bit_adder_2 (
    .sub(sub), .B(B[15:8]), .cin(n8_bit_adder_1_cout), .A(A[15:8]), .overflow(ovf), .result(result[15:8]));  // open: cout
endmodule

module Left_Shifter (
  input  [2:0] shamt,
  input  [15:0] \input ,
  output [15:0] result
);

  wire multiplexer_1_out, multiplexer_2_out, multiplexer_3_out, multiplexer_4_out, multiplexer_5_out,
       multiplexer_6_out, multiplexer_7_out, multiplexer_8_out, multiplexer_9_out, multiplexer_10_out,
       multiplexer_11_out, multiplexer_12_out, multiplexer_13_out, multiplexer_14_out, multiplexer_15_out,
       multiplexer_16_out, multiplexer_17_out, multiplexer_18_out, multiplexer_19_out, multiplexer_20_out,
       multiplexer_21_out, multiplexer_22_out, multiplexer_23_out, multiplexer_24_out, multiplexer_25_out,
       multiplexer_26_out, multiplexer_27_out, multiplexer_28_out, multiplexer_29_out, multiplexer_30_out,
       multiplexer_31_out, multiplexer_32_out;

  Multiplexer #(.enable("false")) multiplexer_1 (
    .in0(\input [15]), .in1(\input [14]), .out(multiplexer_1_out), .sel(shamt[0]));
  Multiplexer #(.enable("false")) multiplexer_2 (
    .in0(\input [14]), .in1(\input [13]), .out(multiplexer_2_out), .sel(shamt[0]));
  Multiplexer #(.enable("false")) multiplexer_3 (
    .in0(\input [13]), .in1(\input [12]), .out(multiplexer_3_out), .sel(shamt[0]));
  Multiplexer #(.enable("false")) multiplexer_4 (
    .in0(\input [12]), .in1(\input [11]), .out(multiplexer_4_out), .sel(shamt[0]));
  Multiplexer #(.enable("false")) multiplexer_5 (
    .in0(\input [11]), .in1(\input [10]), .out(multiplexer_5_out), .sel(shamt[0]));
  Multiplexer #(.enable("false")) multiplexer_6 (
    .in0(\input [10]), .in1(\input [9]), .out(multiplexer_6_out), .sel(shamt[0]));
  Multiplexer #(.enable("false")) multiplexer_7 (
    .in0(\input [9]), .in1(\input [8]), .out(multiplexer_7_out), .sel(shamt[0]));
  Multiplexer #(.enable("false")) multiplexer_8 (
    .in0(\input [8]), .in1(\input [7]), .out(multiplexer_8_out), .sel(shamt[0]));
  Multiplexer #(.enable("false")) multiplexer_9 (
    .in0(\input [7]), .in1(\input [6]), .out(multiplexer_9_out), .sel(shamt[0]));
  Multiplexer #(.enable("false")) multiplexer_10 (
    .in0(\input [6]), .in1(\input [5]), .out(multiplexer_10_out), .sel(shamt[0]));
  Multiplexer #(.enable("false")) multiplexer_11 (
    .in0(\input [5]), .in1(\input [4]), .out(multiplexer_11_out), .sel(shamt[0]));
  Multiplexer #(.enable("false")) multiplexer_12 (
    .in0(\input [4]), .in1(\input [3]), .out(multiplexer_12_out), .sel(shamt[0]));
  Multiplexer #(.enable("false")) multiplexer_13 (
    .in0(\input [3]), .in1(\input [2]), .out(multiplexer_13_out), .sel(shamt[0]));
  Multiplexer #(.enable("false")) multiplexer_14 (
    .in0(\input [2]), .in1(\input [1]), .out(multiplexer_14_out), .sel(shamt[0]));
  Multiplexer #(.enable("false")) multiplexer_15 (
    .in0(\input [1]), .in1(\input [0]), .out(multiplexer_15_out), .sel(shamt[0]));
  Multiplexer #(.enable("false")) multiplexer_16 (
    .in0(\input [0]), .in1(1'b0), .out(multiplexer_16_out), .sel(shamt[0]));
  Multiplexer #(.enable("false")) multiplexer_17 (
    .in0(multiplexer_1_out), .in1(multiplexer_3_out), .out(multiplexer_17_out), .sel(shamt[1]));
  Multiplexer #(.enable("false")) multiplexer_18 (
    .in0(multiplexer_2_out), .in1(multiplexer_4_out), .out(multiplexer_18_out), .sel(shamt[1]));
  Multiplexer #(.enable("false")) multiplexer_19 (
    .in0(multiplexer_3_out), .in1(multiplexer_5_out), .out(multiplexer_19_out), .sel(shamt[1]));
  Multiplexer #(.enable("false")) multiplexer_20 (
    .in0(multiplexer_4_out), .in1(multiplexer_6_out), .out(multiplexer_20_out), .sel(shamt[1]));
  Multiplexer #(.enable("false")) multiplexer_21 (
    .in0(multiplexer_5_out), .in1(multiplexer_7_out), .out(multiplexer_21_out), .sel(shamt[1]));
  Multiplexer #(.enable("false")) multiplexer_22 (
    .in0(multiplexer_6_out), .in1(multiplexer_8_out), .out(multiplexer_22_out), .sel(shamt[1]));
  Multiplexer #(.enable("false")) multiplexer_23 (
    .in0(multiplexer_7_out), .in1(multiplexer_9_out), .out(multiplexer_23_out), .sel(shamt[1]));
  Multiplexer #(.enable("false")) multiplexer_24 (
    .in0(multiplexer_8_out), .in1(multiplexer_10_out), .out(multiplexer_24_out), .sel(shamt[1]));
  Multiplexer #(.enable("false")) multiplexer_25 (
    .in0(multiplexer_9_out), .in1(multiplexer_11_out), .out(multiplexer_25_out), .sel(shamt[1]));
  Multiplexer #(.enable("false")) multiplexer_26 (
    .in0(multiplexer_10_out), .in1(multiplexer_12_out), .out(multiplexer_26_out), .sel(shamt[1]));
  Multiplexer #(.enable("false")) multiplexer_27 (
    .in0(multiplexer_11_out), .in1(multiplexer_13_out), .out(multiplexer_27_out), .sel(shamt[1]));
  Multiplexer #(.enable("false")) multiplexer_28 (
    .in0(multiplexer_12_out), .in1(multiplexer_14_out), .out(multiplexer_28_out), .sel(shamt[1]));
  Multiplexer #(.enable("false")) multiplexer_29 (
    .in0(multiplexer_13_out), .in1(multiplexer_15_out), .out(multiplexer_29_out), .sel(shamt[1]));
  Multiplexer #(.enable("false")) multiplexer_30 (
    .in0(multiplexer_14_out), .in1(multiplexer_16_out), .out(multiplexer_30_out), .sel(shamt[1]));
  Multiplexer #(.enable("false")) multiplexer_31 (
    .in0(multiplexer_15_out), .in1(1'b0), .out(multiplexer_31_out), .sel(shamt[1]));
  Multiplexer #(.enable("false")) multiplexer_32 (
    .in0(multiplexer_16_out), .in1(1'b0), .out(multiplexer_32_out), .sel(shamt[1]));
  Multiplexer #(.enable("false")) multiplexer_33 (
    .in0(multiplexer_17_out), .in1(multiplexer_21_out), .out(result[15]), .sel(shamt[2]));
  Multiplexer #(.enable("false")) multiplexer_34 (
    .in0(multiplexer_18_out), .in1(multiplexer_22_out), .out(result[14]), .sel(shamt[2]));
  Multiplexer #(.enable("false")) multiplexer_35 (
    .in0(multiplexer_19_out), .in1(multiplexer_23_out), .out(result[13]), .sel(shamt[2]));
  Multiplexer #(.enable("false")) multiplexer_36 (
    .in0(multiplexer_20_out), .in1(multiplexer_24_out), .out(result[12]), .sel(shamt[2]));
  Multiplexer #(.enable("false")) multiplexer_37 (
    .in0(multiplexer_21_out), .in1(multiplexer_25_out), .out(result[11]), .sel(shamt[2]));
  Multiplexer #(.enable("false")) multiplexer_38 (
    .in0(multiplexer_22_out), .in1(multiplexer_26_out), .out(result[10]), .sel(shamt[2]));
  Multiplexer #(.enable("false")) multiplexer_39 (
    .in0(multiplexer_23_out), .in1(multiplexer_27_out), .out(result[9]), .sel(shamt[2]));
  Multiplexer #(.enable("false")) multiplexer_40 (
    .in0(multiplexer_24_out), .in1(multiplexer_28_out), .out(result[8]), .sel(shamt[2]));
  Multiplexer #(.enable("false")) multiplexer_41 (
    .in0(multiplexer_25_out), .in1(multiplexer_29_out), .out(result[7]), .sel(shamt[2]));
  Multiplexer #(.enable("false")) multiplexer_42 (
    .in0(multiplexer_26_out), .in1(multiplexer_30_out), .out(result[6]), .sel(shamt[2]));
  Multiplexer #(.enable("false")) multiplexer_43 (
    .in0(multiplexer_27_out), .in1(multiplexer_31_out), .out(result[5]), .sel(shamt[2]));
  Multiplexer #(.enable("false")) multiplexer_44 (
    .in0(multiplexer_28_out), .in1(multiplexer_32_out), .out(result[4]), .sel(shamt[2]));
  Multiplexer #(.enable("false")) multiplexer_45 (
    .in0(multiplexer_29_out), .in1(1'b0), .out(result[3]), .sel(shamt[2]));
  Multiplexer #(.enable("false")) multiplexer_46 (
    .in0(multiplexer_30_out), .in1(1'b0), .out(result[2]), .sel(shamt[2]));
  Multiplexer #(.enable("false")) multiplexer_47 (
    .in0(multiplexer_31_out), .in1(1'b0), .out(result[1]), .sel(shamt[2]));
  Multiplexer #(.enable("false")) multiplexer_48 (
    .in0(multiplexer_32_out), .in1(1'b0), .out(result[0]), .sel(shamt[2]));
endmodule

module Right_Shifter (
  input  [2:0] shamt,
  input  [15:0] \input ,
  output [15:0] result
);

  wire multiplexer_1_out, multiplexer_2_out, multiplexer_3_out, multiplexer_4_out, multiplexer_5_out,
       multiplexer_6_out, multiplexer_7_out, multiplexer_8_out, multiplexer_9_out, multiplexer_10_out,
       multiplexer_11_out, multiplexer_12_out, multiplexer_13_out, multiplexer_14_out, multiplexer_15_out,
       multiplexer_16_out, multiplexer_17_out, multiplexer_18_out, multiplexer_19_out, multiplexer_20_out,
       multiplexer_21_out, multiplexer_22_out, multiplexer_23_out, multiplexer_24_out, multiplexer_25_out,
       multiplexer_26_out, multiplexer_27_out, multiplexer_28_out, multiplexer_29_out, multiplexer_30_out,
       multiplexer_31_out, multiplexer_32_out;

  Multiplexer #(.enable("false")) multiplexer_1 (
    .in0(\input [0]), .in1(\input [1]), .out(multiplexer_1_out), .sel(shamt[0]));
  Multiplexer #(.enable("false")) multiplexer_2 (
    .in0(\input [1]), .in1(\input [2]), .out(multiplexer_2_out), .sel(shamt[0]));
  Multiplexer #(.enable("false")) multiplexer_3 (
    .in0(\input [2]), .in1(\input [3]), .out(multiplexer_3_out), .sel(shamt[0]));
  Multiplexer #(.enable("false")) multiplexer_4 (
    .in0(\input [3]), .in1(\input [4]), .out(multiplexer_4_out), .sel(shamt[0]));
  Multiplexer #(.enable("false")) multiplexer_5 (
    .in0(\input [4]), .in1(\input [5]), .out(multiplexer_5_out), .sel(shamt[0]));
  Multiplexer #(.enable("false")) multiplexer_6 (
    .in0(\input [5]), .in1(\input [6]), .out(multiplexer_6_out), .sel(shamt[0]));
  Multiplexer #(.enable("false")) multiplexer_7 (
    .in0(\input [6]), .in1(\input [7]), .out(multiplexer_7_out), .sel(shamt[0]));
  Multiplexer #(.enable("false")) multiplexer_8 (
    .in0(\input [7]), .in1(\input [8]), .out(multiplexer_8_out), .sel(shamt[0]));
  Multiplexer #(.enable("false")) multiplexer_9 (
    .in0(\input [8]), .in1(\input [9]), .out(multiplexer_9_out), .sel(shamt[0]));
  Multiplexer #(.enable("false")) multiplexer_10 (
    .in0(\input [9]), .in1(\input [10]), .out(multiplexer_10_out), .sel(shamt[0]));
  Multiplexer #(.enable("false")) multiplexer_11 (
    .in0(\input [10]), .in1(\input [11]), .out(multiplexer_11_out), .sel(shamt[0]));
  Multiplexer #(.enable("false")) multiplexer_12 (
    .in0(\input [11]), .in1(\input [12]), .out(multiplexer_12_out), .sel(shamt[0]));
  Multiplexer #(.enable("false")) multiplexer_13 (
    .in0(\input [12]), .in1(\input [13]), .out(multiplexer_13_out), .sel(shamt[0]));
  Multiplexer #(.enable("false")) multiplexer_14 (
    .in0(\input [13]), .in1(\input [14]), .out(multiplexer_14_out), .sel(shamt[0]));
  Multiplexer #(.enable("false")) multiplexer_15 (
    .in0(\input [14]), .in1(\input [15]), .out(multiplexer_15_out), .sel(shamt[0]));
  Multiplexer #(.enable("false")) multiplexer_16 (
    .in0(\input [15]), .in1(\input [15]), .out(multiplexer_16_out), .sel(shamt[0]));
  Multiplexer #(.enable("false")) multiplexer_17 (
    .in0(multiplexer_1_out), .in1(multiplexer_3_out), .out(multiplexer_17_out), .sel(shamt[1]));
  Multiplexer #(.enable("false")) multiplexer_18 (
    .in0(multiplexer_2_out), .in1(multiplexer_4_out), .out(multiplexer_18_out), .sel(shamt[1]));
  Multiplexer #(.enable("false")) multiplexer_19 (
    .in0(multiplexer_3_out), .in1(multiplexer_5_out), .out(multiplexer_19_out), .sel(shamt[1]));
  Multiplexer #(.enable("false")) multiplexer_20 (
    .in0(multiplexer_4_out), .in1(multiplexer_6_out), .out(multiplexer_20_out), .sel(shamt[1]));
  Multiplexer #(.enable("false")) multiplexer_21 (
    .in0(multiplexer_5_out), .in1(multiplexer_7_out), .out(multiplexer_21_out), .sel(shamt[1]));
  Multiplexer #(.enable("false")) multiplexer_22 (
    .in0(multiplexer_6_out), .in1(multiplexer_8_out), .out(multiplexer_22_out), .sel(shamt[1]));
  Multiplexer #(.enable("false")) multiplexer_23 (
    .in0(multiplexer_7_out), .in1(multiplexer_9_out), .out(multiplexer_23_out), .sel(shamt[1]));
  Multiplexer #(.enable("false")) multiplexer_24 (
    .in0(multiplexer_8_out), .in1(multiplexer_10_out), .out(multiplexer_24_out), .sel(shamt[1]));
  Multiplexer #(.enable("false")) multiplexer_25 (
    .in0(multiplexer_9_out), .in1(multiplexer_11_out), .out(multiplexer_25_out), .sel(shamt[1]));
  Multiplexer #(.enable("false")) multiplexer_26 (
    .in0(multiplexer_10_out), .in1(multiplexer_12_out), .out(multiplexer_26_out), .sel(shamt[1]));
  Multiplexer #(.enable("false")) multiplexer_27 (
    .in0(multiplexer_11_out), .in1(multiplexer_13_out), .out(multiplexer_27_out), .sel(shamt[1]));
  Multiplexer #(.enable("false")) multiplexer_28 (
    .in0(multiplexer_12_out), .in1(multiplexer_14_out), .out(multiplexer_28_out), .sel(shamt[1]));
  Multiplexer #(.enable("false")) multiplexer_29 (
    .in0(multiplexer_13_out), .in1(multiplexer_15_out), .out(multiplexer_29_out), .sel(shamt[1]));
  Multiplexer #(.enable("false")) multiplexer_30 (
    .in0(multiplexer_14_out), .in1(multiplexer_16_out), .out(multiplexer_30_out), .sel(shamt[1]));
  Multiplexer #(.enable("false")) multiplexer_31 (
    .in0(multiplexer_15_out), .in1(\input [15]), .out(multiplexer_31_out), .sel(shamt[1]));
  Multiplexer #(.enable("false")) multiplexer_32 (
    .in0(multiplexer_16_out), .in1(\input [15]), .out(multiplexer_32_out), .sel(shamt[1]));
  Multiplexer #(.enable("false")) multiplexer_33 (
    .in0(multiplexer_17_out), .in1(multiplexer_21_out), .out(result[0]), .sel(shamt[2]));
  Multiplexer #(.enable("false")) multiplexer_34 (
    .in0(multiplexer_18_out), .in1(multiplexer_22_out), .out(result[1]), .sel(shamt[2]));
  Multiplexer #(.enable("false")) multiplexer_35 (
    .in0(multiplexer_19_out), .in1(multiplexer_23_out), .out(result[2]), .sel(shamt[2]));
  Multiplexer #(.enable("false")) multiplexer_36 (
    .in0(multiplexer_20_out), .in1(multiplexer_24_out), .out(result[3]), .sel(shamt[2]));
  Multiplexer #(.enable("false")) multiplexer_37 (
    .in0(multiplexer_21_out), .in1(multiplexer_25_out), .out(result[4]), .sel(shamt[2]));
  Multiplexer #(.enable("false")) multiplexer_38 (
    .in0(multiplexer_22_out), .in1(multiplexer_26_out), .out(result[5]), .sel(shamt[2]));
  Multiplexer #(.enable("false")) multiplexer_39 (
    .in0(multiplexer_23_out), .in1(multiplexer_27_out), .out(result[6]), .sel(shamt[2]));
  Multiplexer #(.enable("false")) multiplexer_40 (
    .in0(multiplexer_24_out), .in1(multiplexer_28_out), .out(result[7]), .sel(shamt[2]));
  Multiplexer #(.enable("false")) multiplexer_41 (
    .in0(multiplexer_25_out), .in1(multiplexer_29_out), .out(result[8]), .sel(shamt[2]));
  Multiplexer #(.enable("false")) multiplexer_42 (
    .in0(multiplexer_26_out), .in1(multiplexer_30_out), .out(result[9]), .sel(shamt[2]));
  Multiplexer #(.enable("false")) multiplexer_43 (
    .in0(multiplexer_27_out), .in1(multiplexer_31_out), .out(result[10]), .sel(shamt[2]));
  Multiplexer #(.enable("false")) multiplexer_44 (
    .in0(multiplexer_28_out), .in1(multiplexer_32_out), .out(result[11]), .sel(shamt[2]));
  Multiplexer #(.enable("false")) multiplexer_45 (
    .in0(multiplexer_29_out), .in1(\input [15]), .out(result[12]), .sel(shamt[2]));
  Multiplexer #(.enable("false")) multiplexer_46 (
    .in0(multiplexer_30_out), .in1(\input [15]), .out(result[13]), .sel(shamt[2]));
  Multiplexer #(.enable("false")) multiplexer_47 (
    .in0(multiplexer_31_out), .in1(\input [15]), .out(result[14]), .sel(shamt[2]));
  Multiplexer #(.enable("false")) multiplexer_48 (
    .in0(multiplexer_32_out), .in1(\input [15]), .out(result[15]), .sel(shamt[2]));
endmodule

module Register (
  input  reset,
  input  enable,
  input  clock,
  input  [15:0] \input ,
  output [15:0] result
);

  D_Flip_Flop d_ff_1 (.clk(clock), .D(\input [0]), .Q(result[0]), .en(enable), .reset(reset));  // open: Qn, preset
  D_Flip_Flop d_ff_2 (.clk(clock), .D(\input [1]), .Q(result[1]), .en(enable), .reset(reset));  // open: Qn, preset
  D_Flip_Flop d_ff_3 (.clk(clock), .D(\input [2]), .Q(result[2]), .en(enable), .reset(reset));  // open: Qn, preset
  D_Flip_Flop d_ff_4 (.clk(clock), .D(\input [3]), .Q(result[3]), .en(enable), .reset(reset));  // open: Qn, preset
  D_Flip_Flop d_ff_5 (.clk(clock), .D(\input [4]), .Q(result[4]), .en(enable), .reset(reset));  // open: Qn, preset
  D_Flip_Flop d_ff_6 (.clk(clock), .D(\input [5]), .Q(result[5]), .en(enable), .reset(reset));  // open: Qn, preset
  D_Flip_Flop d_ff_7 (.clk(clock), .D(\input [6]), .Q(result[6]), .en(enable), .reset(reset));  // open: Qn, preset
  D_Flip_Flop d_ff_8 (.clk(clock), .D(\input [7]), .Q(result[7]), .en(enable), .reset(reset));  // open: Qn, preset
  D_Flip_Flop d_ff_9 (.clk(clock), .D(\input [8]), .Q(result[8]), .en(enable), .reset(reset));  // open: Qn, preset
  D_Flip_Flop d_ff_10 (.clk(clock), .D(\input [9]), .Q(result[9]), .en(enable), .reset(reset));  // open: Qn, preset
  D_Flip_Flop d_ff_11 (.clk(clock), .D(\input [10]), .Q(result[10]), .en(enable), .reset(reset));  // open: Qn, preset
  D_Flip_Flop d_ff_12 (.clk(clock), .D(\input [11]), .Q(result[11]), .en(enable), .reset(reset));  // open: Qn, preset
  D_Flip_Flop d_ff_13 (.clk(clock), .D(\input [12]), .Q(result[12]), .en(enable), .reset(reset));  // open: Qn, preset
  D_Flip_Flop d_ff_14 (.clk(clock), .D(\input [13]), .Q(result[13]), .en(enable), .reset(reset));  // open: Qn, preset
  D_Flip_Flop d_ff_15 (.clk(clock), .D(\input [14]), .Q(result[14]), .en(enable), .reset(reset));  // open: Qn, preset
  D_Flip_Flop d_ff_16 (.clk(clock), .D(\input [15]), .Q(result[15]), .en(enable), .reset(reset));  // open: Qn, preset
endmodule

module ALU (
  input  [2:0] aluop,
  input  [15:0] input1,
  input  [15:0] input2,
  input  [2:0] shamt,
  output overflow,
  output [15:0] result
);

  wire [15:0] left_shifter_1_result, n16_bit_adder_subtractor_1_result, nand_1_out, right_shifter_1_result,
       xor_1_out;

  _16_bit_adder_subtractor u_16_bit_adder_subtractor_1 (
    .A(input1), .sub(aluop[0]), .B(input2), .ovf(overflow), .result(n16_bit_adder_subtractor_1_result));
  assign xor_1_out = input1 ^ input2;  // XOR_Gate xor_1, 16 bits wide
  Right_Shifter right_shifter_1 (.shamt(shamt), .\input (input1), .result(right_shifter_1_result));
  Left_Shifter left_shifter_1 (.shamt(shamt), .\input (input1), .result(left_shifter_1_result));
  assign nand_1_out = ~(input1 & input2);  // NAND_Gate nand_1, 16 bits wide
  Multiplexer #(.select(3), .width(16), .enable("false")) multiplexer_1 (
    .in0(n16_bit_adder_subtractor_1_result), .in1(n16_bit_adder_subtractor_1_result), .in2(xor_1_out),
    .in3(nand_1_out), .in4(right_shifter_1_result), .in5(left_shifter_1_result), .out(result), .sel(aluop));  // open: in6, in7
endmodule

module regfile (
  input  reset,
  input  enable,
  input  clock,
  input  [15:0] \input ,
  input  [2:0] Rs1,
  input  [2:0] Rd,
  input  [2:0] Rs2,
  output [15:0] result_1,
  output [15:0] result2
);

  wire and_1_out, and_2_out, and_3_out, and_4_out, and_5_out, and_6_out, and_7_out, and_8_out,
       decoder_1_output0, decoder_1_output1, decoder_1_output2, decoder_1_output3, decoder_1_output4,
       decoder_1_output5, decoder_1_output6, decoder_1_output7;
  wire [15:0] regi0_result, regi1_result, regi2_result, regi3_result, regi4_result, regi5_result,
       regi6_result, regi7_result;

  Decoder decoder_1 (
    .\input (Rd), .output0(decoder_1_output0), .output1(decoder_1_output1), .output2(decoder_1_output2),
    .output3(decoder_1_output3), .output4(decoder_1_output4), .output5(decoder_1_output5),
    .output6(decoder_1_output6), .output7(decoder_1_output7));
  and and_1 (and_1_out, enable, decoder_1_output0);
  and and_2 (and_2_out, enable, decoder_1_output1);
  and and_3 (and_3_out, enable, decoder_1_output2);
  and and_4 (and_4_out, enable, decoder_1_output3);
  and and_5 (and_5_out, enable, decoder_1_output4);
  and and_6 (and_6_out, decoder_1_output5, enable);
  and and_7 (and_7_out, decoder_1_output6, enable);
  and and_8 (and_8_out, decoder_1_output7, enable);
  Register regi0 (.reset(reset), .enable(and_1_out), .clock(clock), .\input (\input ), .result(regi0_result));
  Register regi1 (.reset(reset), .enable(and_2_out), .clock(clock), .\input (\input ), .result(regi1_result));
  Register regi2 (.reset(reset), .enable(and_3_out), .clock(clock), .\input (\input ), .result(regi2_result));
  Register regi3 (.reset(reset), .enable(and_4_out), .clock(clock), .\input (\input ), .result(regi3_result));
  Register regi4 (.reset(reset), .enable(and_5_out), .clock(clock), .\input (\input ), .result(regi4_result));
  Register regi5 (.reset(reset), .enable(and_6_out), .clock(clock), .\input (\input ), .result(regi5_result));
  Register regi6 (.reset(reset), .enable(and_7_out), .clock(clock), .\input (\input ), .result(regi6_result));
  Register regi7 (.reset(reset), .enable(and_8_out), .clock(clock), .\input (\input ), .result(regi7_result));
  // Probe on regi7_result
  // Probe on regi6_result
  // Probe on regi5_result
  // Probe on regi4_result
  // Probe on regi3_result
  // Probe on regi2_result
  // Probe on regi1_result
  // Probe on regi0_result
  Multiplexer #(.select(3), .width(16), .enable("false")) multiplexer_1 (
    .in0(regi0_result), .in1(regi1_result), .in2(regi2_result), .in3(regi3_result), .in4(regi4_result),
    .in5(regi5_result), .in6(regi6_result), .in7(regi7_result), .out(result_1), .sel(Rs1));
  Multiplexer #(.select(3), .width(16), .enable("false")) multiplexer_2 (
    .in0(regi0_result), .in1(regi1_result), .in2(regi2_result), .in3(regi3_result), .in4(regi4_result),
    .in5(regi5_result), .in6(regi6_result), .in7(regi7_result), .out(result2), .sel(Rs2));
endmodule

module main (
  input  reset
);

  wire aluinb, and_1_out, and_2_out, beqz_or_bgt, beqz_output_1_rs_zerotivity, beqz_signal,
       bgt_difference_detector_1_pos_or_neg, bgt_signal, clock, \input , j, jal, jr, keyboard_1_avail,
       multiplexer_8_out, not_1_out, not_2_out, not_3_out, \output , rdst, slwselect, swselect, we;
  wire [2:0] aluop, multiplexer_3_out, multiplexer_4_out;
  wire [3:0] opcode;
  wire [6:0] from_16_to_7_1_output, keyboard_1_data;
  wire [11:0] address;
  wire [15:0] alu_1_result, alu_2_result, current_PC, extend_rd_to_16_1_output, extended_address,
       invalid_extender_1_output, multiplexer_2_out, multiplexer_5_out, multiplexer_6_out, multiplexer_7_out,
       multiplexer_9_out, multiplexer_10_out, multiplexer_11_out, multiplexer_12_out, newrd_value,
       plus_1_result, ram_1_data, regfile_result2, rsvalue, signextend_output;

  Clock u_clock (.out(clock));
  Register register_1 (.reset(reset), .enable(1'b1), .clock(clock), .\input (multiplexer_12_out), .result(current_PC));
  Keyboard keyboard_1 (.clk(clock), .re(\input ), .clr(reset), .avail(keyboard_1_avail), .data(keyboard_1_data));
  _16_bit_adder_subtractor plus_1 (.A(current_PC), .sub(1'b0), .B(16'h1), .result(plus_1_result));  // open: ovf
  extend_rd_to_16 extend_rd_to_16_1 (.rd(keyboard_1_data), .\output (extend_rd_to_16_1_output));
  invalid_extender invalid_extender_1 (.\output (invalid_extender_1_output));
  Multiplexer #(.width(16), .enable("false")) multiplexer_1 (
    .in0(invalid_extender_1_output), .in1(extend_rd_to_16_1_output), .out(newrd_value), .sel(keyboard_1_avail));
  Multiplexer #(.width(16), .enable("false")) multiplexer_2 (
    .in0(multiplexer_9_out), .in1(plus_1_result), .out(multiplexer_2_out), .sel(jal));
  ROM #(.addrWidth(16), .dataWidth(16)) rom_1 (.addr(current_PC), .data({opcode, address}));  // open: sel
  Multiplexer #(.width(3), .enable("false")) multiplexer_3 (
    .in0(multiplexer_4_out), .in1(address[8:6]), .out(multiplexer_3_out), .sel(rdst));
  Multiplexer #(.width(3), .enable("false")) multiplexer_4 (
    .in0(address[5:3]), .in1(3'b111), .out(multiplexer_4_out), .sel(jal));
  not not_1 (not_1_out, clock);
  Multiplexer #(.width(16), .enable("false")) multiplexer_5 (
    .in0(multiplexer_2_out), .in1(newrd_value), .out(multiplexer_5_out), .sel(\input ));
  control control_1 (
    .opcode(opcode), .aluop(aluop), .rdst(rdst), .we(we), .alu_in_b(aluinb), .s_lwselect(slwselect),
    .swselect(swselect), .beqz(beqz_signal), .bgt(bgt_signal), .beqz_or_bgt(beqz_or_bgt), .j(j), .jr(jr),
    .jal(jal), .\input (\input ), .\output (\output ));
  not not_2 (not_2_out, clock);
  regfile regfile (
    .reset(reset), .enable(we), .clock(not_1_out), .\input (multiplexer_5_out), .Rs1(address[11:9]),
    .Rd(multiplexer_3_out), .Rs2(address[8:6]), .result_1(rsvalue), .result2(regfile_result2));
  from_16_to_7 from_16_to_7_1 (.\input (rsvalue), .\output (from_16_to_7_1_output));
  TTY #(.rows(13), .cols(80), .trigger("falling")) tty_1 (
    .data(from_16_to_7_1_output), .clk(not_2_out), .we(\output ), .clr(reset));
  Sign_extender signextend (.\input (address[5:0]), .\output (signextend_output));
  ALU alu_1 (
    .aluop(3'b000), .input1(plus_1_result), .input2(signextend_output), .result(alu_1_result));  // open: shamt, overflow
  Multiplexer #(.width(16), .enable("false")) multiplexer_6 (
    .in0(regfile_result2), .in1(signextend_output), .out(multiplexer_6_out), .sel(aluinb));
  ALU alu_2 (
    .aluop(aluop), .input1(rsvalue), .input2(multiplexer_6_out), .shamt(address[2:0]), .result(alu_2_result));  // open: overflow
  bgt_difference_detector bgt_difference_detector_1 (
    .\input (alu_2_result), .pos_or_neg(bgt_difference_detector_1_pos_or_neg));
  beqz_output beqz_output_1 (.rs(rsvalue), .rs_zerotivity(beqz_output_1_rs_zerotivity));
  not not_3 (not_3_out, clock);
  address_PC_extender address_pc_extender_1 (.address(address), .current_PC(current_PC), .\output (extended_address));
  and and_1 (and_1_out, bgt_signal, bgt_difference_detector_1_pos_or_neg);
  RAM #(.addrWidth(16), .dataWidth(16), .bus("separate")) ram_1 (
    .addr(alu_2_result), .din(regfile_result2), .data(ram_1_data), .str(swselect), .clk(not_3_out));  // open: sel, ld, clr
  Multiplexer #(.width(16), .enable("false")) multiplexer_7 (
    .in0(plus_1_result), .in1(alu_1_result), .out(multiplexer_7_out), .sel(multiplexer_8_out));
  Multiplexer #(.enable("false")) multiplexer_8 (
    .in0(and_1_out), .in1(and_2_out), .out(multiplexer_8_out), .sel(beqz_or_bgt));
  Multiplexer #(.width(16), .enable("false")) multiplexer_9 (
    .in0(alu_2_result), .in1(ram_1_data), .out(multiplexer_9_out), .sel(slwselect));
  and and_2 (and_2_out, beqz_signal, beqz_output_1_rs_zerotivity);
  Multiplexer #(.width(16), .enable("false")) multiplexer_10 (
    .in0(multiplexer_7_out), .in1(extended_address), .out(multiplexer_10_out), .sel(j));
  Multiplexer #(.width(16), .enable("false")) multiplexer_11 (
    .in0(multiplexer_10_out), .in1(rsvalue), .out(multiplexer_11_out), .sel(jr));
  Multiplexer #(.width(16), .enable("false")) multiplexer_12 (
    .in0(multiplexer_11_out), .in1(extended_address), .out(multiplexer_12_out), .sel(jal));

  // Other names for the same wires on the sheet: immediate[5:0] = address[5:0]; shamt[2:0] = address[2:0];
  //   rd[2:0] = address[5:3]; rt[2:0] = address[8:6]; rs[2:0] = address[11:9]

  // Notes on the sheet:
  //   contents of rom_1 (hex, n*v repeats v):
  //   20c0 204f 2090 7441 803f d010 5*2490 2481 e400 8206 2441 803f 2271 ce00 2441 803f b016 3488 803f
endmodule

module Decoder (
  input  [2:0] \input ,
  output output0,
  output output1,
  output output2,
  output output3,
  output output4,
  output output5,
  output output6,
  output output7
);

  wire not_1_out, not_2_out, not_3_out;

  not not_1 (not_1_out, \input [0]);
  not not_2 (not_2_out, \input [1]);
  not not_3 (not_3_out, \input [2]);
  and and_1 (output0, not_1_out, not_2_out, not_3_out);
  and and_2 (output1, \input [0], not_2_out, not_3_out);
  and and_3 (output2, not_1_out, \input [1], not_3_out);
  and and_4 (output3, not_3_out, \input [1], \input [0]);
  and and_5 (output4, \input [2], not_2_out, not_1_out);
  and and_6 (output5, \input [2], not_2_out, \input [0]);
  and and_7 (output6, \input [2], \input [1], not_1_out);
  and and_8 (output7, \input [2], \input [1], \input [0]);
endmodule

module Sign_extender (
  input  [5:0] \input ,
  output [15:0] \output 
);


  assign \output  = {{11{\input [5]}}, \input [4:0]};
endmodule

module control (
  input  [3:0] opcode,
  output \output ,
  output bgt,
  output beqz_or_bgt,
  output j,
  output jr,
  output jal,
  output \input ,
  output alu_in_b,
  output s_lwselect,
  output swselect,
  output beqz,
  output rdst,
  output we,
  output [2:0] aluop
);

  wire ADD, ADDI, BEQZ_t, BGT_t, INPUT_t, J_t, JAL_t, JR_t, LW, NAND, OUTPUT_t, SHL, SHRA, SUB, SW, XOR;

  and u_NAND (NAND, ~opcode[3], ~opcode[2], ~opcode[1], ~opcode[0]);  // AND_Gate
  and u_XOR (XOR, ~opcode[3], ~opcode[2], ~opcode[1], opcode[0]);  // AND_Gate
  or ALU_Op2 (aluop[2], SHRA, SHL);
  and u_ADDI (ADDI, ~opcode[3], ~opcode[2], opcode[1], ~opcode[0]);  // AND_Gate
  and u_ADD (ADD, ~opcode[3], ~opcode[2], opcode[1], opcode[0]);  // AND_Gate
  or ALU_OP1 (aluop[1], NAND, XOR);
  and u_SUB (SUB, ~opcode[3], opcode[2], ~opcode[1], ~opcode[0]);  // AND_Gate
  and u_SHRA (SHRA, ~opcode[3], opcode[2], ~opcode[1], opcode[0]);  // AND_Gate
  or ALU_OP0 (aluop[0], NAND, SUB, SHL, BGT_t);
  and u_SHL (SHL, ~opcode[3], opcode[2], opcode[1], ~opcode[0]);  // AND_Gate
  and u_BGT (BGT_t, ~opcode[3], opcode[2], opcode[1], opcode[0]);  // AND_Gate
  and u_BEQZ (BEQZ_t, opcode[3], ~opcode[2], ~opcode[1], ~opcode[0]);  // AND_Gate
  and u_LW (LW, opcode[3], ~opcode[2], ~opcode[1], opcode[0]);  // AND_Gate
  or u_RDST (rdst, ADDI, LW, SW);
  and u_SW (SW, opcode[3], ~opcode[2], opcode[1], ~opcode[0]);  // AND_Gate
  and u_J (J_t, opcode[3], ~opcode[2], opcode[1], opcode[0]);  // AND_Gate
  or u_we (we, NAND, XOR, ADDI, ADD, SUB, SHRA, SHL, LW, INPUT_t, JAL_t);
  and u_JR (JR_t, opcode[3], opcode[2], ~opcode[1], ~opcode[0]);  // AND_Gate
  and u_JAL (JAL_t, opcode[3], opcode[2], ~opcode[1], opcode[0]);  // AND_Gate
  and u_OUTPUT (OUTPUT_t, opcode[3], opcode[2], opcode[1], ~opcode[0]);  // AND_Gate
  and u_INPUT (INPUT_t, opcode[3], opcode[2], opcode[1], opcode[0]);
  or u_ALU_in_B (alu_in_b, ADDI, LW, SW);
  or u_S_Lwselect (s_lwselect, LW, SW);
  buf u_Swselect (swselect, SW);  // OR_Gate
  buf beqz_signal (beqz, BEQZ_t);  // OR_Gate
  buf bgt_signal (bgt, BGT_t);  // OR_Gate
  buf u_beqz_or_bgt (beqz_or_bgt, BEQZ_t);  // OR_Gate
  buf j_2 (j, J_t);  // OR_Gate
  buf jr_2 (jr, JR_t);  // OR_Gate
  buf jal_2 (jal, JAL_t);  // OR_Gate
  buf input_2 (\input , INPUT_t);  // OR_Gate
  buf output_2 (\output , OUTPUT_t);  // OR_Gate
endmodule

module bgt_difference_detector (
  input  [15:0] \input ,
  output pos_or_neg
);

  wire nor_1_out, or_1_out, xor_1_out;

  or or_1 (or_1_out, \input [0], \input [1], \input [2], \input [3], \input [4], \input [5], \input [6], \input [7], \input [8], \input [9], \input [10], \input [11], \input [12], \input [13], \input [14]);
  xor xor_1 (xor_1_out, or_1_out, \input [15]);
  nor nor_1 (nor_1_out, \input [15], 1'b0);
  and and_1 (pos_or_neg, xor_1_out, nor_1_out);
endmodule

module beqz_output (
  input  [15:0] rs,
  output rs_zerotivity
);

  nor nor_1 (rs_zerotivity, rs[0], rs[1], rs[2], rs[3], rs[4], rs[5], rs[6], rs[7], rs[8], rs[9], rs[10], rs[11], rs[12], rs[13], rs[14], rs[15]);
endmodule

module extend_rd_to_16 (
  input  [6:0] rd,
  output [15:0] \output 
);


  assign \output  = {{9{1'b0}}, rd};
endmodule

module from_16_to_7 (
  input  [15:0] \input ,
  output [6:0] \output 
);


  assign \output  = \input [6:0];
endmodule

// extender for invalid
module invalid_extender (
  output [15:0] \output 
);


  assign \output  = 16'h80;
endmodule

module address_PC_extender (
  input  [11:0] address,
  input  [15:0] current_PC,
  output [15:0] \output 
);


  assign \output  = {current_PC[15:12], address};
endmodule
